// Logisim project Five-Staged-Pipeline-Processor.circ as structural Verilog: 19 circuits, main circuit main
module main (
  input  [3:0] Register_Number,
  input  Reset,
  output [31:0] out_3,
  output [31:0] out_4,
  output [31:0] out_5,
  output [31:0] out_6,
  output [31:0] out_7,
  output [1:0] out_8,
  output [1:0] out_9
);

  wire Clock_out, ex_ma_1_callo, ex_ma_1_wbo, isBeq2, isBeq3, isBgt2, isBgt3, isBranchTaken3, isCall2,
       isCall5, isImmediate2, isLd2, isLd4, isLd5, isLUhaz, isRet2, isRet3, isSt2, isSt4, isUbranch2,
       isUbranch3, isWb2, isWb5, of_ex_1_callo, of_ex_1_ldo, of_ex_1_sto, of_ex_1_wbo, Op_haz, or_1_out,
       RW_MA_haz, RW_OF_src1, RW_OF_src2;
  wire [3:0] Address5, aluSignals2, aluSignals3, of_1_displayout_2, of_1_displayout_3, of_1_displayout_4;
  wire [23:0] branchTarget3, ex_ma_1_pco, of_ex_1_pco, PC1, PC2, PC5;
  wire [31:0] A2, A3, A3_haz, aluResult3, aluResult4, aluResult5, B2, B3, B3_haz, bT2, bT3, ins1_haz,
       ins2_haz, Instruction1, ldResult4, ldResult5, of_1_displayout, op22, op24, op24_haz, opIn, opOut,
       storeData5;

  Clock Clock (.out(Clock_out));
  IF_OF if_of_1 (.PCi(PC1), .Clock(Clock_out), .Insi(ins1_haz), .Pco(PC2), .Inso(out_7));
  bubble bubble_1 (.Ins1(Instruction1), .isBranchTaken(or_1_out), .Ins1_haz(ins1_haz));
  or or_1 (or_1_out, isLUhaz, isBranchTaken3);
  IF if_1 (
    .isBranchTaken(isBranchTaken3), .Instruction(Instruction1), .branchTarget(branchTarget3),
    .IFstageclock(Clock_out), .PC(PC1), .reset(Reset), .isLuHaz(isLUhaz));
  MA ma_1 (.ldResult(ldResult4), .op2(op24_haz), .isLd(isLd4), .isSt(isSt4), .ALUResult(aluResult4), .Clock(Clock_out));
  OF_EX of_ex_1 (
    .Clock(Clock_out), .PCi(PC2), .Sti(isSt2), .Ldi(isLd2), .bTi(bT2), .Beqi(isBeq2), .Bi(B2), .Bgti(isBgt2),
    .Reti(isRet2), .Ai(A2), .op2i(op22), .Wbi(isWb2), .Ubi(isUbranch2), .Insi(ins2_haz), .Calli(isCall2),
    .AluSi(aluSignals2), .PCo(of_ex_1_pco), .Sto(of_ex_1_sto), .Ldo(of_ex_1_ldo), .bTo(bT3), .Beqo(isBeq3),
    .Bo(B3), .Bgto(isBgt3), .Reto(isRet3), .Ao(A3), .op2o(opIn), .Wbo(of_ex_1_wbo), .Ubo(isUbranch3),
    .Inso(out_6), .Callo(of_ex_1_callo), .Aluso(aluSignals3));
  EX_MA ex_ma_1 (
    .Clock(Clock_out), .PCi(of_ex_1_pco), .Sti(of_ex_1_sto), .Ldi(of_ex_1_ldo), .ALUi(aluResult3),
    .op2i(opOut), .Insi(out_6), .Wbi(of_ex_1_wbo), .Calli(of_ex_1_callo), .PCo(ex_ma_1_pco), .Sto(isSt4),
    .Ldo(isLd4), .ALUo(aluResult4), .op2o(op24), .Inso(out_4), .Wbo(ex_ma_1_wbo), .Callo(ex_ma_1_callo));
  MA_WB ma_wb_1 (
    .Clock(Clock_out), .PCi(ex_ma_1_pco), .Ldi(isLd4), .ALUi(aluResult4), .IDi(ldResult4), .Insi(out_4),
    .Wbi(ex_ma_1_wbo), .Calli(ex_ma_1_callo), .PCo(PC5), .Ldo(isLd5), .ALUo(aluResult5), .IDo(ldResult5),
    .Inso(out_3), .Wbo(isWb5), .Callo(isCall5));
  bubble bubble_2 (.Ins1(out_7), .isBranchTaken(isBranchTaken3), .Ins1_haz(ins2_haz));
  OF of_1 (
    .Instruction(ins2_haz), .PC(PC2), .branchTarget(bT2), .isSt(isSt2), .isImmx(isImmediate2), .A(A2),
    .B(B2), .op2(op22), .isRet(isRet2), .writeData(storeData5), .writeAddress(Address5), .isWb(isWb5),
    .clock(Clock_out), .displayAddress(Register_Number),
    .displayOut({of_1_displayout[31:24], of_1_displayout_4, of_1_displayout[19:16], of_1_displayout_3, of_1_displayout[11:8], of_1_displayout_2, of_1_displayout[3:0]}),
    .isCall(isCall5), .RW_OF_src1(RW_OF_src1), .RW_OF_src2(RW_OF_src2), .storeData(storeData5));
  EXU exu_1 (
    .isBeq(isBeq3), .isUbranch(isUbranch3), .isBgt(isBgt3), .branchTargetIn(bT3), .A(A3_haz),
    .aluSignals(aluSignals3), .B(B3_haz), .Clock(Clock_out), .isBranchTaken(isBranchTaken3),
    .branchTargetOut(branchTarget3), .ALUResult(aluResult3), .isRet(isRet3));
  RW rw_1 (
    .Instruction(out_3), .ldResult(ldResult5), .isLd(isLd5), .ALUResult(aluResult5), .isCall(isCall5),
    .PC(PC5), .Address(Address5), .storeData(storeData5));
  Hex_Digit_Display hex_digit_display_1 (.value(of_1_displayout[31:28]));  // open: dp
  Hex_Digit_Display hex_digit_display_2 (.value(of_1_displayout_4));  // open: dp
  Hex_Digit_Display hex_digit_display_3 (.value(of_1_displayout[27:24]));  // open: dp
  CU cu_1 (
    .isWb(isWb2), .isUbranch(isUbranch2), .isImmediate(isImmediate2), .isLd(isLd2), .isSt(isSt2),
    .isBeq(isBeq2), .isBgt(isBgt2), .isCall(isCall2), .isRet(isRet2), .ALUSignals(aluSignals2),
    .Instruction(ins2_haz));
  Forwarding_Unit forwarding_unit_1 (
    .IF_OF(out_7), .OF_EX(out_6), .EX_MA(out_4), .MA_RW(out_3), .RW_MA_src1(RW_MA_haz),
    .RW_OF_src2(RW_OF_src2), .RW_OF_src1(RW_OF_src1), .EX_src_1(out_8), .EX_src_2(out_9), .OP2_line(Op_haz));
  Hex_Digit_Display hex_digit_display_4 (.value(of_1_displayout_3));  // open: dp
  Hex_Digit_Display hex_digit_display_5 (.value(of_1_displayout[19:16]));  // open: dp
  dataLockUnit datalockunit_1 (.Ins_A(Instruction1), .Ins_B(out_7), .out_3(isLUhaz));
  Hex_Digit_Display hex_digit_display_6 (.value(of_1_displayout[11:8]));  // open: dp
  Hex_Digit_Display hex_digit_display_7 (.value(of_1_displayout_2));  // open: dp
  Hex_Digit_Display hex_digit_display_8 (.value(of_1_displayout[3:0]));  // open: dp
  ForwardingValues Forwarding_Unit_Value (
    .storeData5(storeData5), .aluResult4(aluResult4), .op24(op24), .opIn(opIn), .RW_MA_haz(RW_MA_haz),
    .Op_haz(Op_haz), .B3(B3), .A3(A3), .EX_src_2(out_9), .EX_src_1(out_8), .op24_haz(op24_haz),
    .B3_haz(B3_haz), .opOut(opOut), .A3_haz(A3_haz));

  assign out_5 = out_3;

  // Other names for the same wires on the sheet: EX_src_1[1:0] = out_8; EX_src_2[1:0] = out_9;
  //   Instruction2[31:0] = out_7; Instruction3[31:0] = out_6; Instruction4[31:0] = out_4; Instruction5[31:0] = out_3

  // Notes on the sheet:
  //   IF-OF Latch
  //   OF-EX Latch
  //   EX-MA Latch
  //   MA-RW Latch
  //   Note: The last instruction should be provided as "ffffffff" otherwise it will keep on interpreting "00000000", i.e. it will keep on doubling r0.
  //   Five Stage Pipeline Processor
  //   Forwarding, Data-Lock and Branch Unit
  //   Arnab Haldar 2023EET2756
  //   Ranjan Kumar Singha 2023EET2192
  //   Forwarding Unit
endmodule

module IF (
  input  [23:0] branchTarget,
  input  isBranchTaken,
  input  IFstageclock,
  input  reset,
  input  isLuHaz,
  output [31:0] Instruction,
  output [23:0] PC
);

  wire and_1_out, and_2_out, isNB, multiplexer_1_out, not_1_out, or_1_out;

  not not_1 (not_1_out, IFstageclock);
  not not_2 (isNB, isBranchTaken);
  Multiplexer #(.enable("false")) multiplexer_1 (.in0(not_1_out), .in1(1'b1), .out(multiplexer_1_out), .sel(or_1_out));
  or or_1 (or_1_out, and_1_out, isLuHaz);
  Counter #(.width(24), .max('hffffff)) counter_1 (
    .load(isBranchTaken), .D(branchTarget), .count(isNB), .Q(PC), .clk(multiplexer_1_out), .clr(reset));  // open: carry
  and and_1 (and_1_out, and_2_out, isNB);
  ROM #(.addrWidth(24), .dataWidth(32)) rom_1 (.addr(PC), .data(Instruction));  // open: sel
  and and_2 (and_2_out, Instruction[31], Instruction[30], Instruction[29], Instruction[28], Instruction[27], Instruction[26], Instruction[25], Instruction[24], Instruction[23], Instruction[22], Instruction[21], Instruction[20], Instruction[19], Instruction[18], Instruction[17], Instruction[16], Instruction[14], Instruction[13], Instruction[12], Instruction[11], Instruction[10], Instruction[9], Instruction[8], Instruction[7], Instruction[6], Instruction[5], Instruction[4], Instruction[3], Instruction[2], Instruction[1], Instruction[0], Instruction[15]);

  // Notes on the sheet:
  //   reset: pull=down
  //   IF Stage
  //   Counter for going to the next instruction
  //   Note: The last instruction should be provided as "ffffffff" otherwise it will keep on interpreting "00000000", i.e. it will keep on doubling r0.
  //   contents of rom_1 (hex, n*v repeats v):
  //   4c00000a 98000002 90000000 2c000001 88000003 4c400001 a0000000 fb80008 7c380000 7ff80004 c000001
  //   9ffffff8 77f80004 74380000 7b80008 10404000 a0000000 ffffffff
  //   Used to stop instruction processing on encountering code "ffffffff".
endmodule

module OF (
  input  isRet,
  input  RW_OF_src1,
  input  [23:0] PC,
  input  isImmx,
  input  [31:0] Instruction,
  input  isCall,
  input  [3:0] writeAddress,
  input  [31:0] writeData,
  input  isWb,
  input  clock,
  input  isSt,
  input  [3:0] displayAddress,
  input  RW_OF_src2,
  input  [31:0] storeData,
  output [31:0] A,
  output [31:0] op2,
  output [31:0] B,
  output [31:0] displayOut,
  output [31:0] branchTarget
);

  wire and_1_out, or_1_out;
  wire [3:0] multiplexer_2_out, multiplexer_3_out;
  wire [31:0] A_t, adder_1_out, bit_extender_1_out, bit_extender_2_out, bit_extender_3_out,
       bit_extender_4_out, immx, op2_t, shifter_1_out;

  assign bit_extender_1_out = {{5{Instruction[26]}}, Instruction[26:0]};  // Bit_Extender bit_extender_1
  assign bit_extender_2_out = {{8{1'b0}}, PC};  // Bit_Extender bit_extender_2
  Multiplexer #(.width(32), .enable("false")) multiplexer_1 (
    .in0(adder_1_out), .in1(A_t), .out(branchTarget), .sel(isRet));
  Adder #(.width(32)) adder_1 (.a(bit_extender_1_out), .b(bit_extender_2_out), .out(adder_1_out));  // open: cin, cout
  assign bit_extender_3_out = {{16{Instruction[15]}}, Instruction[15:0]};  // Bit_Extender bit_extender_3
  assign bit_extender_4_out = {{16{1'b0}}, Instruction[15:0]};  // Bit_Extender bit_extender_4
  Shifter #(.width(32)) shifter_1 (.in(bit_extender_4_out), .\dist (5'b10000), .out(shifter_1_out));
  Multiplexer #(.width(4), .enable("false")) multiplexer_2 (
    .in0(Instruction[21:18]), .in1(4'b1111), .out(multiplexer_2_out), .sel(isRet));
  Multiplexer #(.width(4), .enable("false")) multiplexer_3 (
    .in0(Instruction[17:14]), .in1(Instruction[25:22]), .out(multiplexer_3_out), .sel(isSt));
  Multiplexer #(.select(2), .width(32), .enable("false")) multiplexer_4 (
    .in0(bit_extender_3_out), .in1(bit_extender_4_out), .in2(shifter_1_out), .out(immx),
    .sel(Instruction[17:16]));  // open: in3
  regFile regfile_1 (
    .writeData(writeData), .writeAddress(writeAddress), .clock(and_1_out), .readB(multiplexer_3_out),
    .outB(op2_t), .outA(A_t), .readA(multiplexer_2_out), .displayOut(displayOut), .displayRead(displayAddress));
  and and_1 (and_1_out, or_1_out, clock);
  Multiplexer #(.width(32)) multiplexer_5 (.in0(A_t), .in1(storeData), .out(A), .sel(RW_OF_src1));  // open: en
  or or_1 (or_1_out, isCall, isWb);
  Multiplexer #(.width(32), .enable("false")) multiplexer_6 (.in0(op2), .in1(immx), .out(B), .sel(isImmx));
  Multiplexer #(.width(32)) multiplexer_7 (.in0(op2_t), .in1(storeData), .out(op2), .sel(RW_OF_src2));  // open: en

  // Other names for the same wires on the sheet: op2_haz[31:0] = op2

  // Notes on the sheet:
  //   (Branch Target Calculation)
  //   (27 bit offset)
  //   OF Stage (Edited)
  //   (has Return Address
  //   when instruction is ret)
  //   (Registers from RW Stage moved here to maintain consistency)
  //   rs1
  //   rs2
  //   rd
  //   (modifier bits)
  //   19:22
  //   15:18
  //   23:26
  //   (Immediate Calculation)
  //   (no modifier)
  //   (modifier u)
  //   (modifier h)
  //   (Register Access)
  //   (32 bit modifed immediate)
  //   (OF Outputs)
endmodule

module MA (
  input  [31:0] ALUResult,
  input  isLd,
  input  Clock,
  input  isSt,
  input  [31:0] op2,
  output [31:0] ldResult
);

  wire and_1_out, not_1_out, xor_1_out;
  wire [31:0] shifter_1_out;

  Shifter #(.width(32), .shift("ar")) shifter_1 (.in(ALUResult), .\dist (5'b00010), .out(shifter_1_out));
  and and_1 (and_1_out, isSt, Clock);
  xor xor_1 (xor_1_out, isLd, and_1_out);
  not not_1 (not_1_out, isSt);
  RAM #(.addrWidth(24), .dataWidth(32), .bus("asynch")) ram_1 (
    .addr(shifter_1_out[23:0]), .data(ldResult), .sel(xor_1_out), .ld(not_1_out));  // open: clr
  assign ldResult = isSt ? op2 : 32'bz;  // Controlled_Buffer controlled_buffer_1

  // Notes on the sheet:
  //   MA  Stage
  //   Memory Address
  //   (Data to be stored)
endmodule

module RW (
  input  [31:0] ALUResult,
  input  [31:0] ldResult,
  input  isLd,
  input  [23:0] PC,
  input  isCall,
  input  [31:0] Instruction,
  output [31:0] storeData,
  output [3:0] Address
);

  wire [31:0] adder_1_out, bit_extender_1_out;

  assign bit_extender_1_out = {{8{1'b0}}, PC};  // Bit_Extender bit_extender_1
  Multiplexer #(.width(4), .enable("false")) multiplexer_1 (
    .in0(Instruction[25:22]), .in1(4'b1111), .out(Address), .sel(isCall));
  Adder #(.width(32)) adder_1 (.a(bit_extender_1_out), .b(32'h1), .out(adder_1_out));  // open: cin, cout
  Multiplexer #(.select(2), .width(32), .enable("false")) multiplexer_2 (
    .in0(ALUResult), .in1(ldResult), .in2(adder_1_out), .out(storeData), .sel({isCall, isLd}));  // open: in3

  // Notes on the sheet:
  //   PC: pull=down
  //   Address: pull=down
  //   storeData: pull=down
  //   RW Stage (Edited)
  //   (for arithmetic instructions)
  //   (data loaded from memory)
  //   (to update return address)
  //   (Register to be written to)
  //   (Registers moved to OF Stage to maintain consistency)
  //   (Integer to be written back in register)
endmodule

module regFile (
  input  clock,
  input  [3:0] readA,
  input  [31:0] writeData,
  input  [3:0] readB,
  input  [3:0] writeAddress,
  input  [3:0] displayRead,
  output [31:0] outA,
  output [31:0] outB,
  output [31:0] displayOut
);

  wire counter_1_q;
  wire [31:0] demultiplexer_1_out0, demultiplexer_1_out1, demultiplexer_1_out2, demultiplexer_1_out3,
       demultiplexer_1_out4, demultiplexer_1_out5, demultiplexer_1_out6, demultiplexer_1_out7,
       demultiplexer_1_out8, demultiplexer_1_out9, demultiplexer_1_out10, demultiplexer_1_out11,
       demultiplexer_1_out12, demultiplexer_1_out13, demultiplexer_1_out14, demultiplexer_1_out15,
       multiplexer_1_out, r0, r1, r2, r3, r4, r5, r6, r7, r8, r9, r10, r11, r12, r13, r14, r15;

  Demultiplexer #(.select(4), .width(32), .tristate("true"), .enable("false")) demultiplexer_1 (
    .out0(demultiplexer_1_out0), .out1(demultiplexer_1_out1), .out2(demultiplexer_1_out2),
    .out3(demultiplexer_1_out3), .out4(demultiplexer_1_out4), .out5(demultiplexer_1_out5),
    .out6(demultiplexer_1_out6), .out7(demultiplexer_1_out7), .out8(demultiplexer_1_out8),
    .out9(demultiplexer_1_out9), .out10(demultiplexer_1_out10), .out11(demultiplexer_1_out11),
    .out12(demultiplexer_1_out12), .out13(demultiplexer_1_out13), .out14(demultiplexer_1_out14),
    .out15(demultiplexer_1_out15), .in(writeData), .sel(writeAddress));
  Counter #(.width(1), .max('h1), .ongoal("stay")) counter_1 (
    .Q(counter_1_q), .clk(clock));  // open: load, D, count, carry, clr
  Multiplexer #(.width(32), .enable("false")) multiplexer_1 (
    .in0(32'h3fffffc), .in1(demultiplexer_1_out14), .out(multiplexer_1_out), .sel(counter_1_q));
  Register #(.width(32)) u_r0 (.D(demultiplexer_1_out0), .Q(r0), .clk(clock));  // open: en, clr
  Register #(.width(32)) u_r1 (.D(demultiplexer_1_out1), .Q(r1), .clk(clock));  // open: en, clr
  Register #(.width(32)) u_r2 (.D(demultiplexer_1_out2), .Q(r2), .clk(clock));  // open: en, clr
  Register #(.width(32)) u_r3 (.D(demultiplexer_1_out3), .Q(r3), .clk(clock));  // open: en, clr
  Register #(.width(32)) u_r4 (.D(demultiplexer_1_out4), .Q(r4), .clk(clock));  // open: en, clr
  Register #(.width(32)) u_r5 (.D(demultiplexer_1_out5), .Q(r5), .clk(clock));  // open: en, clr
  Register #(.width(32)) u_r6 (.D(demultiplexer_1_out6), .Q(r6), .clk(clock));  // open: en, clr
  Register #(.width(32)) u_r7 (.D(demultiplexer_1_out7), .Q(r7), .clk(clock));  // open: en, clr
  Register #(.width(32)) u_r8 (.D(demultiplexer_1_out8), .Q(r8), .clk(clock));  // open: en, clr
  Register #(.width(32)) u_r9 (.D(demultiplexer_1_out9), .Q(r9), .clk(clock));  // open: en, clr
  Register #(.width(32)) u_r10 (.D(demultiplexer_1_out10), .Q(r10), .clk(clock));  // open: en, clr
  Register #(.width(32)) u_r11 (.D(demultiplexer_1_out11), .Q(r11), .clk(clock));  // open: en, clr
  Register #(.width(32)) u_r12 (.D(demultiplexer_1_out12), .Q(r12), .clk(clock));  // open: en, clr
  Register #(.width(32)) u_r13 (.D(demultiplexer_1_out13), .Q(r13), .clk(clock));  // open: en, clr
  Register #(.width(32)) u_r14 (.D(multiplexer_1_out), .Q(r14), .clk(clock));  // open: en, clr
  Register #(.width(32)) u_r15 (.D(demultiplexer_1_out15), .Q(r15), .clk(clock));  // open: en, clr
  Multiplexer #(.select(4), .width(32), .disabled(0), .enable("false")) multiplexer_2 (
    .in0(r0), .in1(r1), .in2(r2), .in3(r3), .in4(r4), .in5(r5), .in6(r6), .in7(r7), .in8(r8), .in9(r9),
    .in10(r10), .in11(r11), .in12(r12), .in13(r13), .in14(r14), .in15(r15), .out(outA), .sel(readA));
  Multiplexer #(.select(4), .width(32), .disabled(0), .enable("false")) multiplexer_3 (
    .in0(r0), .in1(r1), .in2(r2), .in3(r3), .in4(r4), .in5(r5), .in6(r6), .in7(r7), .in8(r8), .in9(r9),
    .in10(r10), .in11(r11), .in12(r12), .in13(r13), .in14(r14), .in15(r15), .out(outB), .sel(readB));
  Multiplexer #(.select(4), .width(32), .disabled(0), .enable("false")) multiplexer_4 (
    .in0(r0), .in1(r1), .in2(r2), .in3(r3), .in4(r4), .in5(r5), .in6(r6), .in7(r7), .in8(r8), .in9(r9),
    .in10(r10), .in11(r11), .in12(r12), .in13(r13), .in14(r14), .in15(r15), .out(displayOut),
    .sel(displayRead));

  // Notes on the sheet:
  //   readA: pull=down
  //   writeAddress: pull=down
  //   displayOut: pull=down
  //   outB: pull=down
  //   displayRead: pull=down
  //   writeData: pull=down
  //   outA: pull=down
  //   readB: pull=down
  //   (for RW Stage)
  //   (to initialize stack pointer
  //   to last memory location)
  //   (to fetch Operand 1)
  //   (to fetch Operand 2)
  //   (for external display)
endmodule

module CU (
  input  [31:0] Instruction,
  output isWb,
  output isUbranch,
  output isImmediate,
  output isLd,
  output isSt,
  output isBeq,
  output isBgt,
  output isCall,
  output isRet,
  output [3:0] ALUSignals
);

  wire and_1_out, and_2_out, and_3_out, and_4_out, demultiplexer_1_out0, demultiplexer_1_out1, isAdd, isAnd,
       isAsr, isCmp, isDiv, isLsl, isLsr, isMod, isMov, isMul, isNot, isOr, not_1_out, not_2_out, not_3_out,
       not_4_out, not_5_out, not_6_out, not_7_out, or_1_out, or_2_out;
  wire [3:0] adder_1_out, adder_2_out, adder_3_out, adder_4_out, adder_5_out, adder_6_out, adder_7_out,
       adder_8_out, adder_9_out, adder_10_out, adder_11_out, bit_extender_1_out, bit_extender_2_out,
       bit_extender_3_out, bit_extender_4_out, bit_extender_5_out, bit_extender_6_out, bit_extender_7_out,
       bit_extender_8_out, bit_extender_9_out, bit_extender_10_out, bit_extender_11_out, bit_extender_12_out,
       bit_extender_13_out, multiplier_1_out, multiplier_2_out, multiplier_3_out, multiplier_4_out,
       multiplier_5_out, multiplier_6_out, multiplier_7_out, multiplier_8_out, multiplier_9_out,
       multiplier_10_out, multiplier_11_out, multiplier_12_out;

  not not_1 (not_1_out, Instruction[28]);
  not not_2 (not_2_out, Instruction[29]);
  not not_3 (not_3_out, Instruction[28]);
  not not_4 (not_4_out, Instruction[27]);
  not not_5 (not_5_out, Instruction[31]);
  Demultiplexer #(.select(5), .disabled(0), .enable("false")) demultiplexer_1 (
    .out0(demultiplexer_1_out0), .out1(demultiplexer_1_out1), .out2(isMul), .out3(isDiv), .out4(isMod),
    .out5(isCmp), .out6(isAnd), .out7(isOr), .out8(isNot), .out9(isMov), .out10(isLsl), .out11(isLsr),
    .out12(isAsr), .out14(isLd), .out15(isSt), .out16(isBeq), .out17(isBgt), .out19(isCall), .out20(isRet),
    .in(1'b1), .sel(Instruction[31:27]));  // open: out13, out18, out21, out22, out23, out24, out25, out26, out27, out28, out29, out30, out31
  not not_6 (not_6_out, Instruction[31]);
  or or_1 (or_1_out, Instruction[30], not_1_out);
  and and_1 (and_1_out, not_2_out, Instruction[28]);
  and and_2 (and_2_out, Instruction[29], not_3_out, not_4_out);
  and and_3 (and_3_out, Instruction[28], Instruction[29], Instruction[30], not_5_out);
  and and_4 (and_4_out, not_6_out, Instruction[29], Instruction[27], or_1_out);
  not not_7 (not_7_out, Instruction[30]);
  or or_2 (or_2_out, and_1_out, and_2_out);
  nor nor_1 (isWb, Instruction[31], and_4_out);
  and and_5 (isUbranch, Instruction[31], not_7_out, or_2_out);
  or or_3 (isAdd, and_3_out, demultiplexer_1_out0);
  assign bit_extender_1_out = {{3{1'b0}}, demultiplexer_1_out1};  // Bit_Extender bit_extender_1
  assign bit_extender_2_out = {{3{1'b0}}, isCmp};  // Bit_Extender bit_extender_2
  assign bit_extender_3_out = {{3{1'b0}}, isMul};  // Bit_Extender bit_extender_3
  assign bit_extender_4_out = {{3{1'b0}}, isDiv};  // Bit_Extender bit_extender_4
  assign bit_extender_5_out = {{3{1'b0}}, isMod};  // Bit_Extender bit_extender_5
  assign bit_extender_6_out = {{3{1'b0}}, isLsl};  // Bit_Extender bit_extender_6
  assign bit_extender_7_out = {{3{1'b0}}, isLsr};  // Bit_Extender bit_extender_7
  assign bit_extender_8_out = {{3{1'b0}}, isAsr};  // Bit_Extender bit_extender_8
  assign bit_extender_9_out = {{3{1'b0}}, isOr};  // Bit_Extender bit_extender_9
  assign bit_extender_10_out = {{3{1'b0}}, isNot};  // Bit_Extender bit_extender_10
  assign bit_extender_11_out = {{3{1'b0}}, isAnd};  // Bit_Extender bit_extender_11
  assign bit_extender_12_out = {{3{1'b0}}, isMov};  // Bit_Extender bit_extender_12
  assign bit_extender_13_out = {{3{1'b0}}, isAdd};  // Bit_Extender bit_extender_13
  Multiplier #(.width(4)) multiplier_1 (
    .a(bit_extender_1_out), .b(4'b0010), .out(multiplier_1_out));  // open: cin, cout
  Multiplier #(.width(4)) multiplier_2 (
    .a(bit_extender_2_out), .b(4'b0011), .out(multiplier_2_out));  // open: cin, cout
  Multiplier #(.width(4)) multiplier_3 (
    .a(bit_extender_3_out), .b(4'b0100), .out(multiplier_3_out));  // open: cin, cout
  Multiplier #(.width(4)) multiplier_4 (
    .a(bit_extender_4_out), .b(4'b0101), .out(multiplier_4_out));  // open: cin, cout
  Multiplier #(.width(4)) multiplier_5 (
    .a(bit_extender_5_out), .b(4'b0110), .out(multiplier_5_out));  // open: cin, cout
  Multiplier #(.width(4)) multiplier_6 (
    .a(bit_extender_6_out), .b(4'b0111), .out(multiplier_6_out));  // open: cin, cout
  Multiplier #(.width(4)) multiplier_7 (
    .a(bit_extender_7_out), .b(4'b1000), .out(multiplier_7_out));  // open: cin, cout
  Multiplier #(.width(4)) multiplier_8 (
    .a(bit_extender_8_out), .b(4'b1001), .out(multiplier_8_out));  // open: cin, cout
  Multiplier #(.width(4)) multiplier_9 (
    .a(bit_extender_9_out), .b(4'b1010), .out(multiplier_9_out));  // open: cin, cout
  Multiplier #(.width(4)) multiplier_10 (
    .a(bit_extender_10_out), .b(4'b1011), .out(multiplier_10_out));  // open: cin, cout
  Multiplier #(.width(4)) multiplier_11 (
    .a(bit_extender_11_out), .b(4'b1100), .out(multiplier_11_out));  // open: cin, cout
  Multiplier #(.width(4)) multiplier_12 (
    .a(bit_extender_12_out), .b(4'b1101), .out(multiplier_12_out));  // open: cin, cout
  Adder #(.width(4)) adder_1 (.a(bit_extender_13_out), .b(multiplier_1_out), .out(adder_1_out));  // open: cin, cout
  Adder #(.width(4)) adder_2 (.a(multiplier_2_out), .b(multiplier_3_out), .out(adder_2_out));  // open: cin, cout
  Adder #(.width(4)) adder_3 (.a(multiplier_4_out), .b(multiplier_5_out), .out(adder_3_out));  // open: cin, cout
  Adder #(.width(4)) adder_4 (.a(multiplier_6_out), .b(multiplier_7_out), .out(adder_4_out));  // open: cin, cout
  Adder #(.width(4)) adder_5 (.a(multiplier_8_out), .b(multiplier_9_out), .out(adder_5_out));  // open: cin, cout
  Adder #(.width(4)) adder_6 (.a(multiplier_10_out), .b(multiplier_11_out), .out(adder_6_out));  // open: cin, cout
  Adder #(.width(4)) adder_7 (.a(adder_1_out), .b(adder_2_out), .out(adder_7_out));  // open: cin, cout
  Adder #(.width(4)) adder_8 (.a(adder_3_out), .b(adder_4_out), .out(adder_8_out));  // open: cin, cout
  Adder #(.width(4)) adder_9 (.a(adder_5_out), .b(adder_6_out), .out(adder_9_out));  // open: cin, cout
  Adder #(.width(4)) adder_10 (.a(adder_7_out), .b(adder_8_out), .out(adder_10_out));  // open: cin, cout
  Adder #(.width(4)) adder_11 (.a(adder_9_out), .b(multiplier_12_out), .out(adder_11_out));  // open: cin, cout
  Adder #(.width(4)) adder_12 (.a(adder_10_out), .b(adder_11_out), .out(ALUSignals));  // open: cin, cout

  assign isImmediate = Instruction[26];

  // Notes on the sheet:
  //   Instruction: pull=down
  //   opcode
  //   (Circuit for signals created by multiple instructions)
  //   (Demultiplexer for Control Signals created by single instructions)
  //   Create ALUSignals
endmodule

module ALU (
  input  [31:0] A,
  input  [3:0] aluSignals,
  input  [31:0] B,
  input  clock,
  output [31:0] aluResult,
  output flags_GT,
  output flags_E
);

  wire [31:0] Add, addA, addB, And, andA, andB, Asr, asrA, asrB, cmpA, cmpB, Div, divA, divB, Lsl, lslA,
       lslB, Lsr, lsrA, lsrB, Mod, modA, modB, movB, Mul, mulA, mulB, Not, notB, Or, orA, orB, register_1_q,
       register_2_q, Sub, subA, subB;

  Demultiplexer #(.select(4), .width(32), .tristate("true"), .enable("false")) demultiplexer_1 (
    .out1(addA), .out2(subA), .out3(cmpA), .out4(mulA), .out5(divA), .out6(modA), .out7(lslA), .out8(lsrA),
    .out9(asrA), .out10(orA), .out12(andA), .in(A), .sel(aluSignals));  // open: out0, out11, out13, out14, out15
  Demultiplexer #(.select(4), .width(32), .tristate("true"), .disabled(0), .enable("false")) demultiplexer_2 (
    .out1(addB), .out2(subB), .out3(cmpB), .out4(mulB), .out5(divB), .out6(modB), .out7(lslB), .out8(lsrB),
    .out9(asrB), .out10(orB), .out11(notB), .out12(andB), .out13(movB), .in(B), .sel(aluSignals));  // open: out0, out14, out15
  Adder #(.width(32)) adder_1 (.a(addA), .b(addB), .out(Add));  // open: cin, cout
  Subtractor #(.width(32)) subtractor_1 (.a(subA), .b(subB), .out(Sub));  // open: bin, bout
  Shifter #(.width(32)) shifter_1 (.in(lslA), .\dist (lslB[4:0]), .out(Lsl));
  Shifter #(.width(32), .shift("lr")) shifter_2 (.in(lsrA), .\dist (lsrB[4:0]), .out(Lsr));
  Shifter #(.width(32), .shift("ar")) shifter_3 (.in(asrA), .\dist (asrB[4:0]), .out(Asr));
  Register #(.width(32)) register_1 (.D(cmpA), .Q(register_1_q), .clk(clock));  // open: en, clr
  Register #(.width(32)) register_2 (.D(cmpB), .Q(register_2_q), .clk(clock));  // open: en, clr
  Comparator #(.width(32)) comparator_1 (.a(register_1_q), .b(register_2_q), .gt(flags_GT), .eq(flags_E));  // open: lt
  Multiplier #(.width(32)) multiplier_1 (.a(mulA), .b(mulB), .out(Mul));  // open: cin, cout
  Divider #(.width(32)) divider_1 (.a(divA), .b(divB), .out(Div));  // open: upper, rem
  Divider #(.width(32)) divider_2 (.a(modA), .b(modB), .rem(Mod));  // open: out, upper
  Multiplexer #(.select(4), .width(32), .disabled(0)) multiplexer_1 (
    .in1(Add), .in2(Sub), .in4(Mul), .in5(Div), .in6(Mod), .in7(Lsl), .in8(Lsr), .in9(Asr), .in10(Or),
    .in11(Not), .in12(And), .in13(movB), .out(aluResult), .sel(aluSignals), .en(1'b1));  // open: in0, in3, in14, in15
  assign Or = orA | orB;  // OR_Gate or_1, 32 bits wide
  assign And = andA & andB;  // AND_Gate and_1, 32 bits wide
  assign Not = ~notB;  // NOT_Gate not_1, 32 bits wide

  // Notes on the sheet:
  //   flags_E: pull=down
  //   B: pull=down
  //   A: pull=down
  //   flags_GT: pull=down
  //   aluResult: pull=down
  //   Operand 1
  //   Operand 2
  //   Provide operands to their respective functions.
  //   Compare instruction needs registers as we need to keep the value of the flags stored.
endmodule

module EXU (
  input  isBeq,
  input  isUbranch,
  input  isBgt,
  input  isRet,
  input  [31:0] branchTargetIn,
  input  [31:0] A,
  input  [3:0] aluSignals,
  input  [31:0] B,
  input  Clock,
  output isBranchTaken,
  output [23:0] branchTargetOut,
  output [31:0] ALUResult
);

  wire and_1_out, and_2_out, flags_E, flags_GT;
  wire [31:24] multiplexer_1_out;

  and and_1 (and_1_out, isBeq, flags_E);
  and and_2 (and_2_out, isBgt, flags_GT);
  ALU alu_1 (
    .A(A), .aluSignals(aluSignals), .B(B), .clock(Clock), .aluResult(ALUResult), .flags_GT(flags_GT),
    .flags_E(flags_E));
  Multiplexer #(.width(32), .enable("false")) multiplexer_1 (
    .in0(branchTargetIn), .in1(A), .out({multiplexer_1_out, branchTargetOut}), .sel(isRet));
  or or_1 (isBranchTaken, and_1_out, isUbranch, and_2_out);

  // Notes on the sheet:
  //   branchTargetIn: pull=down
  //   aluSignals: pull=down
  //   ALUResult: pull=down
  //   isBgt: pull=down
  //   branchTargetOut: pull=down
  //   isBeq: pull=down
  //   B: pull=down
  //   isUbranch: pull=down
  //   isBranchTaken: pull=down
  //   A: pull=down
  //   (Operand 1)
  //   (Operand 2)
  //   EX Stage
  //   (To be sent to the IF Stage)
endmodule

module IF_OF (
  input  [23:0] PCi,
  input  Clock,
  input  [31:0] Insi,
  output [23:0] Pco,
  output [31:0] Inso
);

  Register #(.width(24), .trigger("falling")) PC (.D(PCi), .Q(Pco), .clk(Clock));  // open: en, clr
  Register #(.width(32), .trigger("falling")) Instruction (.D(Insi), .Q(Inso), .clk(Clock));  // open: en, clr
endmodule

module OF_EX (
  input  Clock,
  input  [23:0] PCi,
  input  Sti,
  input  Ldi,
  input  [31:0] bTi,
  input  Beqi,
  input  [31:0] Bi,
  input  Bgti,
  input  Reti,
  input  [31:0] Ai,
  input  [31:0] op2i,
  input  Wbi,
  input  Ubi,
  input  [31:0] Insi,
  input  Calli,
  input  [3:0] AluSi,
  output [23:0] PCo,
  output Sto,
  output Ldo,
  output [31:0] bTo,
  output Beqo,
  output [31:0] Bo,
  output Bgto,
  output Reto,
  output [31:0] Ao,
  output [31:0] op2o,
  output Wbo,
  output Ubo,
  output [31:0] Inso,
  output Callo,
  output [3:0] Aluso
);

  Register #(.width(24), .trigger("falling")) PC (.D(PCi), .Q(PCo), .clk(Clock));  // open: en, clr
  Register #(.width(32), .trigger("falling")) branchTarget (.D(bTi), .Q(bTo), .clk(Clock));  // open: en, clr
  Register #(.width(32), .trigger("falling")) B (.D(Bi), .Q(Bo), .clk(Clock));  // open: en, clr
  Register #(.width(32), .trigger("falling")) A (.D(Ai), .Q(Ao), .clk(Clock));  // open: en, clr
  Register #(.width(32), .trigger("falling")) op2 (.D(op2i), .Q(op2o), .clk(Clock));  // open: en, clr
  Register #(.width(32), .trigger("falling")) Instruction (.D(Insi), .Q(Inso), .clk(Clock));  // open: en, clr
  Register #(.width(4), .trigger("falling")) AluSignals (.D(AluSi), .Q(Aluso), .clk(Clock));  // open: en, clr
  Register #(.width(1), .trigger("falling")) isSt (.D(Sti), .Q(Sto), .clk(Clock));  // open: en, clr
  Register #(.width(1), .trigger("falling")) isLd (.D(Ldi), .Q(Ldo), .clk(Clock));  // open: en, clr
  Register #(.width(1), .trigger("falling")) isBeq (.D(Beqi), .Q(Beqo), .clk(Clock));  // open: en, clr
  Register #(.width(1), .trigger("falling")) isBgt (.D(Bgti), .Q(Bgto), .clk(Clock));  // open: en, clr
  Register #(.width(1), .trigger("falling")) isRet (.D(Reti), .Q(Reto), .clk(Clock));  // open: en, clr
  Register #(.width(1), .trigger("falling")) isWb (.D(Wbi), .Q(Wbo), .clk(Clock));  // open: en, clr
  Register #(.width(1), .trigger("falling")) isUbranch (.D(Ubi), .Q(Ubo), .clk(Clock));  // open: en, clr
  Register #(.width(1), .trigger("falling")) isCall (.D(Calli), .Q(Callo), .clk(Clock));  // open: en, clr
endmodule

module EX_MA (
  input  Clock,
  input  [23:0] PCi,
  input  Sti,
  input  Ldi,
  input  [31:0] ALUi,
  input  [31:0] op2i,
  input  [31:0] Insi,
  input  Wbi,
  input  Calli,
  output [23:0] PCo,
  output Sto,
  output Ldo,
  output [31:0] ALUo,
  output [31:0] op2o,
  output [31:0] Inso,
  output Wbo,
  output Callo
);

  Register #(.width(24), .trigger("falling")) PC (.D(PCi), .Q(PCo), .clk(Clock));  // open: en, clr
  Register #(.width(32), .trigger("falling")) AluResult (.D(ALUi), .Q(ALUo), .clk(Clock));  // open: en, clr
  Register #(.width(32), .trigger("falling")) op2 (.D(op2i), .Q(op2o), .clk(Clock));  // open: en, clr
  Register #(.width(32), .trigger("falling")) Instruction (.D(Insi), .Q(Inso), .clk(Clock));  // open: en, clr
  Register #(.width(1), .trigger("falling")) isSt (.D(Sti), .Q(Sto), .clk(Clock));  // open: en, clr
  Register #(.width(1), .trigger("falling")) isLd (.D(Ldi), .Q(Ldo), .clk(Clock));  // open: en, clr
  Register #(.width(1), .trigger("falling")) isWb (.D(Wbi), .Q(Wbo), .clk(Clock));  // open: en, clr
  Register #(.width(1), .trigger("falling")) isCall (.D(Calli), .Q(Callo), .clk(Clock));  // open: en, clr
endmodule

module MA_WB (
  input  Clock,
  input  [23:0] PCi,
  input  Ldi,
  input  [31:0] ALUi,
  input  [31:0] IDi,
  input  [31:0] Insi,
  input  Wbi,
  input  Calli,
  output [23:0] PCo,
  output Ldo,
  output [31:0] ALUo,
  output [31:0] IDo,
  output [31:0] Inso,
  output Wbo,
  output Callo
);

  Register #(.width(24), .trigger("falling")) PC (.D(PCi), .Q(PCo), .clk(Clock));  // open: en, clr
  Register #(.width(32), .trigger("falling")) AluResult (.D(ALUi), .Q(ALUo), .clk(Clock));  // open: en, clr
  Register #(.width(32), .trigger("falling")) idResult (.D(IDi), .Q(IDo), .clk(Clock));  // open: en, clr
  Register #(.width(32), .trigger("falling")) Instruction (.D(Insi), .Q(Inso), .clk(Clock));  // open: en, clr
  Register #(.width(1), .trigger("falling")) isLd (.D(Ldi), .Q(Ldo), .clk(Clock));  // open: en, clr
  Register #(.width(1), .trigger("falling")) isWb (.D(Wbi), .Q(Wbo), .clk(Clock));  // open: en, clr
  Register #(.width(1), .trigger("falling")) isCall (.D(Calli), .Q(Callo), .clk(Clock));  // open: en, clr
endmodule

module Forwarding_Unit (
  input  [31:0] IF_OF,
  input  [31:0] OF_EX,
  input  [31:0] EX_MA,
  input  [31:0] MA_RW,
  output RW_MA_src1,
  output RW_OF_src2,
  output RW_OF_src1,
  output OP2_line,
  output [1:0] EX_src_1,
  output [1:0] EX_src_2
);

  wire comparator_3_eq, isSt, MA1, MA1_in, MA2_in, or_1_out;

  rs2_rd_conf rs2_rd_conf_1 (.Ins_A(IF_OF), .Ins_B(MA_RW), .out_3(RW_OF_src2));
  rs2_rd_conf rs2_rd_conf_2 (.Ins_A(OF_EX), .Ins_B(EX_MA), .out_3(MA1_in));
  rs1_rd_conf rs1_rd_conf_1 (.Ins_A(IF_OF), .Ins_B(MA_RW), .out_3(RW_OF_src1));
  and and_1 (EX_src_2[1], ~isSt, MA1);  // AND_Gate
  and and_2 (EX_src_2[0], ~isSt, OP2_line);  // AND_Gate
  rs1_rd_conf rs1_rd_conf_2 (.Ins_A(OF_EX), .Ins_B(EX_MA), .out_3(MA2_in));
  rs2_rd_conf rs2_rd_conf_3 (.Ins_A(OF_EX), .Ins_B(MA_RW), .out_3(OP2_line));
  rs1_rd_conf rs1_rd_conf_3 (.Ins_A(OF_EX), .Ins_B(MA_RW), .out_3(EX_src_1[0]));
  Comparator #(.width(5)) comparator_1 (.a(5'b01111), .b(OF_EX[31:27]), .eq(isSt));  // open: gt, lt
  Comparator #(.width(5)) comparator_2 (.a(EX_MA[31:27]), .b(5'b01001));  // open: gt, eq, lt
  rs2_rd_conf rs2_rd_conf_4 (.Ins_A(EX_MA), .Ins_B(MA_RW), .out_3(RW_MA_src1));
  Comparator #(.width(5)) comparator_3 (.a(EX_MA[31:27]), .b(5'b01110), .eq(comparator_3_eq));  // open: gt, lt
  or or_1 (or_1_out, comparator_3_eq, 1'b0);
  Multiplexer multiplexer_1 (.in0(MA1_in), .in1(1'b0), .out(MA1), .sel(or_1_out));  // open: en
  Multiplexer multiplexer_2 (.in0(MA2_in), .in1(1'b0), .out(EX_src_1[1]), .sel(or_1_out));  // open: en

  // Other names for the same wires on the sheet: MA2 = EX_src_1[1]

  // Notes on the sheet:
  //   RW-OF rs2 conflict
  //         MA-EX rs2 conflict
  //   RW-OF rs1 conflict
  //            EX-MA rs1 conflict
  //   RW-EX rs2 conflict
  //   RW-EX rs1 conflict
  //       RW-MA conflict
endmodule

module rs1_rd_conf (
  input  [31:0] Ins_A,
  input  [31:0] Ins_B,
  output out_3
);

  wire comparator_1_eq, comparator_2_eq, comparator_3_eq, comparator_4_eq, comparator_5_eq, comparator_6_eq,
       comparator_7_eq, comparator_8_eq, comparator_9_eq, comparator_10_eq, comparator_11_eq,
       comparator_12_eq, comparator_13_eq, comparator_14_eq, comparator_15_eq, comparator_16_eq,
       comparator_17_eq, comparator_18_eq, nor_1_out, nor_2_out, not_1_out;
  wire [3:0] multiplexer_1_out, multiplexer_2_out;

  Comparator #(.width(5)) comparator_1 (.a(Ins_A[31:27]), .b(5'b01101), .eq(comparator_1_eq));  // open: gt, lt
  Comparator #(.width(5)) comparator_2 (.a(Ins_A[31:27]), .b(5'b10010), .eq(comparator_2_eq));  // open: gt, lt
  Comparator #(.width(5)) comparator_3 (.a(Ins_A[31:27]), .b(5'b10000), .eq(comparator_3_eq));  // open: gt, lt
  Comparator #(.width(5)) comparator_4 (.a(Ins_A[31:27]), .b(5'b10001), .eq(comparator_4_eq));  // open: gt, lt
  Comparator #(.width(5)) comparator_5 (.a(Ins_A[31:27]), .b(5'b10011), .eq(comparator_5_eq));  // open: gt, lt
  Comparator #(.width(5)) comparator_6 (.a(Ins_A[31:27]), .b(5'b01000), .eq(comparator_6_eq));  // open: gt, lt
  Comparator #(.width(5)) comparator_7 (.a(Ins_A[31:27]), .b(5'b01001), .eq(comparator_7_eq));  // open: gt, lt
  Comparator #(.width(5)) comparator_8 (.a(Ins_A[31:27]), .b(5'b10100), .eq(comparator_8_eq));  // open: gt, lt
  Comparator #(.width(5)) comparator_9 (.a(5'b10011), .b(Ins_B[31:27]), .eq(comparator_9_eq));  // open: gt, lt
  Comparator #(.width(5)) comparator_10 (.a(Ins_B[31:27]), .b(5'b01101), .eq(comparator_10_eq));  // open: gt, lt
  Comparator #(.width(5)) comparator_11 (.a(Ins_B[31:27]), .b(5'b00101), .eq(comparator_11_eq));  // open: gt, lt
  Comparator #(.width(5)) comparator_12 (.a(Ins_B[31:27]), .b(5'b01111), .eq(comparator_12_eq));  // open: gt, lt
  Comparator #(.width(5)) comparator_13 (.a(Ins_B[31:27]), .b(5'b10010), .eq(comparator_13_eq));  // open: gt, lt
  Comparator #(.width(5)) comparator_14 (.a(Ins_B[31:27]), .b(5'b10000), .eq(comparator_14_eq));  // open: gt, lt
  Comparator #(.width(5)) comparator_15 (.a(Ins_B[31:27]), .b(5'b10001), .eq(comparator_15_eq));  // open: gt, lt
  Comparator #(.width(5)) comparator_16 (.a(Ins_B[31:27]), .b(5'b10100), .eq(comparator_16_eq));  // open: gt, lt
  Comparator #(.width(32)) comparator_17 (.a(Ins_B), .b({32{1'b0}}), .eq(comparator_17_eq));  // open: gt, lt
  nor nor_1 (nor_1_out, comparator_1_eq, comparator_2_eq, comparator_3_eq, comparator_4_eq, comparator_5_eq, comparator_6_eq, comparator_7_eq);
  Multiplexer #(.width(4)) multiplexer_1 (
    .in0(Ins_A[21:18]), .in1(4'b1111), .out(multiplexer_1_out), .sel(comparator_8_eq));  // open: en
  Multiplexer #(.width(4)) multiplexer_2 (
    .in0(Ins_B[25:22]), .in1(4'b1111), .out(multiplexer_2_out), .sel(comparator_9_eq));  // open: en
  nor nor_2 (nor_2_out, comparator_10_eq, comparator_11_eq, comparator_12_eq, comparator_13_eq, comparator_14_eq, comparator_15_eq, comparator_16_eq);
  Comparator #(.width(4)) comparator_18 (
    .a(multiplexer_1_out), .b(multiplexer_2_out), .eq(comparator_18_eq));  // open: gt, lt
  not not_1 (not_1_out, comparator_17_eq);
  and and_1 (out_3, nor_1_out, comparator_18_eq, nor_2_out, not_1_out);
endmodule

module rs2_rd_conf (
  input  [31:0] Ins_A,
  input  [31:0] Ins_B,
  output out_3
);

  wire comparator_1_eq, comparator_2_eq, comparator_3_eq, comparator_4_eq, comparator_5_eq, comparator_6_eq,
       comparator_7_eq, comparator_8_eq, comparator_9_eq, comparator_10_eq, comparator_11_eq,
       comparator_12_eq, comparator_13_eq, comparator_14_eq, comparator_15_eq, comparator_16_eq, nand_1_out,
       nor_1_out, nor_2_out, not_1_out, not_2_out;
  wire [3:0] multiplexer_1_out, multiplexer_2_out;

  Comparator #(.width(5)) comparator_1 (.a(Ins_A[31:27]), .b(5'b01101), .eq(comparator_1_eq));  // open: gt, lt
  Comparator #(.width(5)) comparator_2 (.a(Ins_A[31:27]), .b(5'b10010), .eq(comparator_2_eq));  // open: gt, lt
  Comparator #(.width(5)) comparator_3 (.a(Ins_A[31:27]), .b(5'b10000), .eq(comparator_3_eq));  // open: gt, lt
  Comparator #(.width(5)) comparator_4 (.a(Ins_A[31:27]), .b(5'b10001), .eq(comparator_4_eq));  // open: gt, lt
  Comparator #(.width(5)) comparator_5 (.a(Ins_A[31:27]), .b(5'b10011), .eq(comparator_5_eq));  // open: gt, lt
  Comparator #(.width(5)) comparator_6 (.a(Ins_A[31:27]), .b(5'b01111), .eq(comparator_6_eq));  // open: gt, lt
  Comparator #(.width(5)) comparator_7 (.a(5'b10011), .b(Ins_B[31:27]), .eq(comparator_7_eq));  // open: gt, lt
  Comparator #(.width(5)) comparator_8 (.a(Ins_B[31:27]), .b(5'b01101), .eq(comparator_8_eq));  // open: gt, lt
  Comparator #(.width(5)) comparator_9 (.a(Ins_B[31:27]), .b(5'b00101), .eq(comparator_9_eq));  // open: gt, lt
  Comparator #(.width(5)) comparator_10 (.a(Ins_B[31:27]), .b(5'b01111), .eq(comparator_10_eq));  // open: gt, lt
  Comparator #(.width(5)) comparator_11 (.a(Ins_B[31:27]), .b(5'b10010), .eq(comparator_11_eq));  // open: gt, lt
  Comparator #(.width(5)) comparator_12 (.a(Ins_B[31:27]), .b(5'b10000), .eq(comparator_12_eq));  // open: gt, lt
  Comparator #(.width(5)) comparator_13 (.a(Ins_B[31:27]), .b(5'b10001), .eq(comparator_13_eq));  // open: gt, lt
  Comparator #(.width(5)) comparator_14 (.a(Ins_B[31:27]), .b(5'b10100), .eq(comparator_14_eq));  // open: gt, lt
  Comparator #(.width(32)) comparator_15 (.a(Ins_B), .b({32{1'b0}}), .eq(comparator_15_eq));  // open: gt, lt
  not not_1 (not_1_out, comparator_6_eq);
  nor nor_1 (nor_1_out, comparator_1_eq, comparator_2_eq, comparator_3_eq, comparator_4_eq, comparator_5_eq);
  Multiplexer #(.width(4)) multiplexer_1 (
    .in0(Ins_A[17:14]), .in1(Ins_A[25:22]), .out(multiplexer_1_out), .sel(comparator_6_eq));  // open: en
  Multiplexer #(.width(4)) multiplexer_2 (
    .in0(Ins_B[25:22]), .in1(4'b1111), .out(multiplexer_2_out), .sel(comparator_7_eq));  // open: en
  nor nor_2 (nor_2_out, comparator_8_eq, comparator_9_eq, comparator_10_eq, comparator_11_eq, comparator_12_eq, comparator_13_eq, comparator_14_eq);
  nand nand_1 (nand_1_out, not_1_out, Ins_A[26]);
  Comparator #(.width(4)) comparator_16 (
    .a(multiplexer_1_out), .b(multiplexer_2_out), .eq(comparator_16_eq));  // open: gt, lt
  not not_2 (not_2_out, comparator_15_eq);
  and and_1 (out_3, nor_1_out, nand_1_out, comparator_16_eq, nor_2_out, not_2_out);
endmodule

// Bubble
module bubble (
  input  [31:0] Ins1,
  input  isBranchTaken,
  output [31:0] Ins1_haz
);

  Multiplexer #(.width(32)) multiplexer_1 (
    .in0(Ins1), .in1(32'h68000000), .out(Ins1_haz), .sel(isBranchTaken));  // open: en
endmodule

// Datalock unit
module dataLockUnit (
  input  [31:0] Ins_A,
  input  [31:0] Ins_B,
  output out_3
);

  wire and_1_out, and_2_out, and_3_out, comparator_1_eq, comparator_2_eq, comparator_3_eq, comparator_4_eq,
       comparator_5_eq, comparator_6_eq, comparator_7_eq, comparator_8_eq, comparator_9_eq, comparator_10_eq,
       comparator_11_eq, comparator_12_eq, comparator_13_eq, comparator_14_eq, nor_1_out, nor_2_out,
       not_1_out, not_2_out, or_1_out, or_2_out;
  wire [3:0] multiplexer_1_out, multiplexer_2_out;

  Comparator #(.width(5)) comparator_1 (.a(Ins_B[31:27]), .b(5'b01110), .eq(comparator_1_eq));  // open: gt, lt
  Comparator #(.width(5)) comparator_2 (.a(Ins_A[31:27]), .b(5'b01101), .eq(comparator_2_eq));  // open: gt, lt
  Comparator #(.width(5)) comparator_3 (.a(Ins_A[31:27]), .b(5'b10010), .eq(comparator_3_eq));  // open: gt, lt
  Comparator #(.width(5)) comparator_4 (.a(Ins_A[31:27]), .b(5'b10000), .eq(comparator_4_eq));  // open: gt, lt
  Comparator #(.width(5)) comparator_5 (.a(Ins_A[31:27]), .b(5'b10001), .eq(comparator_5_eq));  // open: gt, lt
  Comparator #(.width(5)) comparator_6 (.a(Ins_A[31:27]), .b(5'b10011), .eq(comparator_6_eq));  // open: gt, lt
  Comparator #(.width(5)) comparator_7 (.a(Ins_A[31:27]), .b(5'b10100), .eq(comparator_7_eq));  // open: gt, lt
  Comparator #(.width(5)) comparator_8 (.a(Ins_A[31:27]), .b(5'b01111), .eq(comparator_8_eq));  // open: gt, lt
  Comparator #(.width(5)) comparator_9 (.a(Ins_A[31:27]), .b(5'b01000), .eq(comparator_9_eq));  // open: gt, lt
  Comparator #(.width(5)) comparator_10 (.a(Ins_A[31:27]), .b(5'b01001), .eq(comparator_10_eq));  // open: gt, lt
  Comparator #(.width(32)) comparator_11 (.a(Ins_B), .b({32{1'b0}}), .eq(comparator_11_eq));  // open: gt, lt
  Comparator #(.width(32)) comparator_12 (.a(Ins_B), .b({32{1'b1}}), .eq(comparator_12_eq));  // open: gt, lt
  nor nor_1 (nor_1_out, comparator_9_eq, comparator_10_eq);
  not not_1 (not_1_out, comparator_8_eq);
  or or_1 (or_1_out, comparator_11_eq, comparator_12_eq);
  nor nor_2 (nor_2_out, comparator_2_eq, comparator_3_eq, comparator_4_eq, comparator_5_eq, comparator_6_eq);
  Multiplexer #(.width(4)) multiplexer_1 (
    .in0(Ins_A[21:18]), .in1(4'b1111), .out(multiplexer_1_out), .sel(comparator_7_eq));  // open: en
  Multiplexer #(.width(4)) multiplexer_2 (
    .in0(Ins_A[17:14]), .in1(Ins_A[25:22]), .out(multiplexer_2_out), .sel(comparator_8_eq));  // open: en
  and and_1 (and_1_out, not_1_out, Ins_A[26]);
  Comparator #(.width(4)) comparator_13 (
    .a(multiplexer_2_out), .b(Ins_B[25:22]), .eq(comparator_13_eq));  // open: gt, lt
  Comparator #(.width(4)) comparator_14 (
    .a(multiplexer_1_out), .b(Ins_B[25:22]), .eq(comparator_14_eq));  // open: gt, lt
  and and_2 (and_2_out, and_1_out, comparator_13_eq);
  and and_3 (and_3_out, comparator_14_eq, nor_1_out);
  not not_2 (not_2_out, or_1_out);
  or or_2 (or_2_out, and_2_out, and_3_out);
  and and_4 (out_3, nor_2_out, or_2_out, comparator_1_eq, not_2_out);
endmodule

module ForwardingValues (
  input  [31:0] storeData5,
  input  [31:0] aluResult4,
  input  [31:0] op24,
  input  [31:0] opIn,
  input  RW_MA_haz,
  input  Op_haz,
  input  [31:0] B3,
  input  [31:0] A3,
  input  [1:0] EX_src_2,
  input  [1:0] EX_src_1,
  output [31:0] op24_haz,
  output [31:0] opOut,
  output [31:0] B3_haz,
  output [31:0] A3_haz
);

  Multiplexer #(.width(32)) multiplexer_1 (.in0(op24), .in1(storeData5), .out(op24_haz), .sel(RW_MA_haz));  // open: en
  Multiplexer #(.select(2), .width(32)) multiplexer_2 (
    .in0(B3), .in1(storeData5), .in2(aluResult4), .in3(aluResult4), .out(B3_haz), .sel(EX_src_2));  // open: en
  Multiplexer #(.width(32)) multiplexer_3 (.in0(opIn), .in1(storeData5), .out(opOut), .sel(Op_haz));  // open: en
  Multiplexer #(.select(2), .width(32)) multiplexer_4 (
    .in0(A3), .in1(storeData5), .in2(aluResult4), .in3(aluResult4), .out(A3_haz), .sel(EX_src_1));  // open: en
endmodule
